# Fritzing sketch esp-pc-util (saved by Fritzing 0.9.5d)

parts:
  LCD1 = 2.8" SPI TFT Module [part_number=MSP2807]
  RE1 = KY-040 Rotary encoder [package=THT]
  A1 = ESP32-S3-WROOM-1-N16R8 dev board
  S1 = Momentary Switch [package=ksa_sealed_tac_switch]
  S2 = Momentary Switch [package=ksa_sealed_tac_switch]
  S3 = Momentary Switch [package=ksa_sealed_tac_switch]
  J1 = male pin header, 6 pins [form="♂ (male)"]
  J2 = single row smd male pin header, 3 pins [form="♂ (male)"]

nets:
  N1: LCD1.pin1, J2.pin3
  N2: LCD1.pin2, J1.pin6
  N3: LCD1.pin3, A1.Pin_16
  N4: LCD1.pin4, A1.Pin_12
  N5: LCD1.pin5, A1.Pin_15
  N6: LCD1.pin6, A1.Pin_17
  N7: LCD1.pin7, A1.Pin_18
  N8: LCD1.pin8, A1.Pin_11
  N9: LCD1.pin9, A1.Pin_19
  N10: RE1.GND, J1.pin1
  N11: RE1.Vcc, J2.pin2
  N12: RE1.SW, A1.Pin_9
  N13: RE1.DT, A1.Pin_8
  N14: RE1.CLK, A1.Pin_7
  N15: A1.Pin_1, J2.pin1
  N16: A1.Pin_4, S1.3
  N17: A1.Pin_5, S2.3
  N18: A1.Pin_6, S3.3
  N19: A1.Pin_22, A1.Pin_44, J1.pin5
  N20: S1.2, J1.pin2
  N21: S2.2, J1.pin3
  N22: S3.2, J1.pin4

custom parts:
  2.8" SPI TFT Module: A generic 2.8 inch LCD TFT 320x240 display with touchscreen and SD card slot. Uses the ILI9341 controller, like the Adafruit displays of this size uses.
  KY-040 Rotary encoder: KY-040 Rotary Encoder with switch on breakout borad from AZ Delivery
  ESP32-S3-WROOM-1-N16R8 dev board: ESP32-S3 WIFI+BLE5.0 Development Board ESP32-S3-WROOM-1-N16R8(16M Flash/8SRAM).
